# Fritzing sketch connection_diagram (saved by Fritzing 0.9.9b)

parts:
  MH-ET_LIVE_ESP32_DEVKIT1 = MH-ET LIVE ESP32 DEVKIT 38 pins
  S1 = H-Bridge with L298N
  Grove1 = Grove OLED 128x96
  R1 = Rotary Potentiometer (Small) [maximum_resistance=100kΩ package=THT]
  DS1 = DS18B20 1-Wire Temperature Sensor Probe Cable
  J1 = Piezo Speaker
  R2 = Resistor [tolerance=±5% power=0.25 resistance=10k package=THT]
  LED1 = smd LED [color="Green (565nm)" package="0603 [SMD]"]
  R3 = Resistor [tolerance=±5% power=0.25 resistance=220 package=THT]
  LED2 = LEDs [package=led10mm]

nets:
  3V3: MH-ET_LIVE_ESP32_DEVKIT1.3V3, Grove1.VCC, R1.leg1
  N1: MH-ET_LIVE_ESP32_DEVKIT1.IO34, R1.wiper
  N2: MH-ET_LIVE_ESP32_DEVKIT1.IO35, R3.Pin_1
  N3: MH-ET_LIVE_ESP32_DEVKIT1.IO32, DS1.shield, R2.Pin_0
  N4: MH-ET_LIVE_ESP32_DEVKIT1.IO25, S1.IN3
  N5: MH-ET_LIVE_ESP32_DEVKIT1.IO26, S1.IN4
  N6: MH-ET_LIVE_ESP32_DEVKIT1.IO27, S1.ENB
  N7: MH-ET_LIVE_ESP32_DEVKIT1.IO14, J1.pin2
  GND: MH-ET_LIVE_ESP32_DEVKIT1.GND, Grove1.GND, R1.leg2, DS1.GND, J1.pin1
  N8: MH-ET_LIVE_ESP32_DEVKIT1.IO22, Grove1.SCL
  N9: MH-ET_LIVE_ESP32_DEVKIT1.IO21, Grove1.SDA
  N10: S1.M2-01, LED2.C
  N11: S1.M2-02, LED2.A
  N12: LED1.anode, R3.Pin_0

notes:
  Bui Ngoc Long

custom parts:
  MH-ET LIVE ESP32 DEVKIT 38 pins: http://mh.nodebb.com/topic/2/mh-et-live-esp32-devkit
  H-Bridge with L298N: h-bridge
